# Fritzing sketch 01_led_blink (saved by Fritzing 0.9.3b)
circuit board: 8.46667cm x 5.64444cm
breadboards: 1

parts:
  LED1 = LED - 5mm [color="Red (633nm)" package="5 mm [THT]"]
  IC1 = IC, DIP package, 8 pins [chip_label=IC]
  R1 = Resistor [tolerance=±5% resistance=220 package=THT]

nets:
  N1: LED1.cathode, R1.Pin_1
  N2: LED1.anode, IC1.pin5
  N3: IC1.pin8, R1.Pin_0
